# Fritzing sketch Lab1Fzz (saved by Fritzing 0.9.2b)
breadboards: 1

parts:
  R1 = Resistor [tolerance=±5% resistance=330 package=THT]
  R2 = Resistor [tolerance=±5% resistance=330 package=THT]
  R3 = Resistor [tolerance=±5% resistance=330 package=THT]
  LED2 = RGB LED (com. cathode, rgb) [package="5 mm [THT]"]
  Part1 = Arduino Uno (Rev3)
  S1 = Toggle Switch [package=THT]
  R6 = Photocell (LDR) [package=THT]
  R7 = Resistor [tolerance=±5% resistance=10k package=THT]
  LED3 = smd LED [color="Green (570nm)" package="0603 [SMD]"]
  R9 = Resistor [tolerance=±5% resistance=10k package=THT]
  R10 = Resistor [tolerance=±5% resistance=10k package=THT]
  R11 = Resistor [tolerance=±5% resistance=330 package=THT]

nets:
  N1: R1.Pin_0, LED2.red_anode
  N2: R1.Pin_1, Part1.D12/MISO
  N3: R2.Pin_0, LED2.blue_anode
  N4: R2.Pin_1, Part1.D10_PWM/SS
  N5: R3.Pin_0, LED2.green_anode
  N6: R3.Pin_1, Part1.D11_PWM/MOSI
  N7: LED2.common_cathode, Part1.5V, S1.L1, S1.L2, R6.pin_1, LED3.anode
  N8: Part1.A0, R6.pin_0, R7.Pin_1
  N9: Part1.D8, R10.Pin_1
  N10: Part1.D9_PWM, R9.Pin_1
  N11: Part1.D6_PWM, R11.Pin_0
  N12: R7.Pin_0, R9.Pin_0, R10.Pin_0
  N13: LED3.cathode, R11.Pin_1
