# Fritzing sketch lab2 (saved by Fritzing 0.9.2b)
breadboards: 1

parts:
  Part1 = Arduino Uno (Rev3)
  R1 = Resistor [tolerance=±5% resistance=330 package=THT]
  J1 = Piezo Speaker
  7_Segment1 = 7 Segment Display
  R2 = Resistor [tolerance=±5% resistance=330 package=THT]
  R3 = Resistor [tolerance=±5% resistance=330 package=THT]
  R4 = Resistor [tolerance=±5% resistance=330 package=THT]
  R5 = Resistor [tolerance=±5% resistance=330 package=THT]
  R6 = Resistor [tolerance=±5% resistance=330 package=THT]
  R7 = Resistor [tolerance=±5% resistance=330 package=THT]
  R8 = Resistor [tolerance=±5% resistance=330 package=THT]
  R9 = Resistor [tolerance=±5% resistance=330 package=THT]
  R10 = Resistor [tolerance=±5% resistance=330 package=THT]
  LED2 = RGB LED (com. cathode, rgb) [package="5 mm [THT]"]
  R11 = Resistor [tolerance=±5% resistance=330 package=THT]
  R12 = Resistor [tolerance=±5% resistance=330 package=THT]

nets:
  N1: Part1.D8, R3.Pin_1
  N2: Part1.D9_PWM, R6.Pin_0
  N3: Part1.D10_PWM/SS, J1.pin2
  N4: Part1.D11_PWM/MOSI, R12.Pin_1
  N5: Part1.D12/MISO, R11.Pin_1
  N6: Part1.D13/SCK, R10.Pin_1
  N7: Part1.GND, R1.Pin_1
  N8: Part1.D2, R7.Pin_1
  N9: Part1.D3_PWM, R8.Pin_1
  N10: Part1.D4, R9.Pin_1
  N11: Part1.D5_PWM, R2.Pin_1
  N12: Part1.D6_PWM, R4.Pin_1
  N13: Part1.D7, R5.Pin_1
  N14: Part1.5V, 7_Segment1.Segment_G, 7_Segment1.Segment_DP
  N15: R1.Pin_0, J1.pin1
  N16: 7_Segment1.Segment_F, R5.Pin_0
  N17: 7_Segment1.common_anode, R3.Pin_0, R9.Pin_0
  N18: 7_Segment1.Segment_E, R4.Pin_0
  N19: 7_Segment1.Segment_D, R2.Pin_0
  N20: 7_Segment1.Segment_C, R6.Pin_1
  N21: 7_Segment1.Segment_B, R8.Pin_0
  N22: 7_Segment1.Segment_A, R7.Pin_0
  N23: R10.Pin_0, LED2.red_anode
  N24: LED2.green_anode, R11.Pin_0
  N25: LED2.blue_anode, R12.Pin_0
