# Fritzing sketch lab5 (saved by Fritzing 0.9.2b)
breadboards: 1

parts:
  Part1 = Arduino Uno (Rev3)
  T1 = LM35 Temperature Sensor [package="TO92 [THT]"]
  Part2 = SRF05 Ultrasonic Rangefinder

nets:
  N1: Part1.A1, T1.Vout
  N2: Part1.D9_PWM, Part2.Trig
  N3: Part1.D10_PWM/SS, Part2.Echo
  GND: Part1.GND, T1.GND, Part2.GND
  N4: Part1.5V, T1.+Vs
