# Fritzing sketch Project1Fritzing (saved by Fritzing 0.9.2b)
breadboards: 4

parts:
  M1 = DC Motor
  M2 = DC Motor
  VCC1 = 4 x AAA Battery Mount
  J1 = Basic Servo
  Part3 = SRF05 Ultrasonic Rangefinder
  Part4 = 2A MOTOR SHIELD 9
  IR1 = TSOP312.., 314.. [package=THT]
  TCRT6 = TCRT5000 sensor module [part_number=151608]
  TCRT7 = TCRT5000 sensor module [part_number=151608]
  TCRT8 = TCRT5000 sensor module [part_number=151608]
  R7 = Resistor [tolerance=±5% resistance=10k package=THT]
  R8 = Resistor [tolerance=±5% resistance=100 package=THT]
  R9 = Resistor [tolerance=±5% resistance=10k package=THT]
  R10 = Resistor [tolerance=±5% resistance=100 package=THT]
  R11 = Resistor [tolerance=±5% resistance=100 package=THT]
  R12 = Resistor [tolerance=±5% resistance=10k package=THT]
  Part5 = Arduino Uno (Rev3)
  LCD1 = LCD screen
  R13 = Resistor [tolerance=±5% resistance=1k package="0402 [SMD]"]
  R15 = TRIMPOT [package=3362u-2]
  S2 = Momentary Switch [package=ksa_sealed_tac_switch]
  S3 = Momentary Switch [package=ksa_sealed_tac_switch]
  R16 = Resistor [tolerance=±5% resistance=220 package="0805 [SMD]"]
  R17 = Resistor [tolerance=±5% resistance=220 package="0805 [SMD]"]
  S4 = Round Pushbutton
  R18 = Resistor [tolerance=±5% resistance=220 package="0805 [SMD]"]
  Q2 = PNP-Transistor [part_number=3144 package="SOT-23 [SMD]"]
  Q3 = PNP-Transistor [part_number=3144 package="SOT-23 [SMD]"]

nets:
  N1: M1.pin_1, Part4.M2+
  N2: M1.pin_2, Part4.M2-
  N3: M2.pin_1, Part4.M1+
  N4: M2.pin_2, Part4.M1-
  N5: VCC1.-, Part4.GND#0
  N6: VCC1.+, Part4.PWRIN
  GND: J1.gnd, Part3.GND, Part4.GND#connector1pad-4-5-0-39-8-14, IR1.GND, TCRT6.D-, TCRT6.T-, TCRT7.D-, TCRT7.T-, TCRT8.D-, TCRT8.T-, Q2.0, Q3.0
  VCC: J1.vcc, Part3.VCC, Part4.5V, IR1.Vs, R7.Pin_1, R8.Pin_0, R9.Pin_1, R10.Pin_0, R11.Pin_0, R12.Pin_1, Q2.1, Q3.1
  N7: J1.pulse, Part4.D11
  N8: Part3.Trig, Part4.D9
  N9: Part3.Echo, Part4.D8
  N10: Part4.D3, Q3.2
  N11: Part4.A4, Part5.A4/SDA
  N12: Part4.A1, TCRT7.T+, R9.Pin_0
  N13: Part4.A2, TCRT6.T+, R7.Pin_0
  N14: Part4.D2, Q2.2
  N15: Part4.D10, IR1.Data
  N16: Part4.A5, Part5.A5/SCL
  N17: Part4.A0, TCRT8.T+, R12.Pin_0
  N18: Part4.D12, S4.leg0, R18.Pin_0
  N19: TCRT6.D+, R8.Pin_1
  N20: TCRT7.D+, R10.Pin_1
  N21: TCRT8.D+, R11.Pin_1
  N22: Part5.A2, LCD1.E
  N23: Part5.A3, LCD1.RS
  N24: Part5.D8, LCD1.DB7
  N25: Part5.D9_PWM, LCD1.DB6
  N26: Part5.D10_PWM/SS, LCD1.DB5
  N27: Part5.D11_PWM/MOSI, LCD1.DB4
  N28: Part5.D2, S2.1, R16.Pin_0
  N29: Part5.D3_PWM, S3.1, R17.Pin_0
  5V: Part5.5V, LCD1.VDD, R13.Pin_1, R15.CCW, S2.3, S3.3, S4.leg1
  GND_2: Part5.GND, LCD1.VSS, LCD1.R/W, LCD1.LED-, R15.CW, R16.Pin_1, R17.Pin_1, R18.Pin_1
  N30: LCD1.V0, R15.WIPER
  N31: LCD1.LED+, R13.Pin_0

custom parts:
  TCRT5000 sensor module: breakout board with TCRT5000
