# Fritzing sketch project2 (saved by Fritzing 0.9.2b)
breadboards: 2

parts:
  Part1 = Arduino Uno (Rev3)
  R7 = PHOTOCELL [package=photocell]
  R8 = PHOTOCELL [package=photocell]
  R9 = PHOTOCELL [package=photocell]
  R10 = Resistor [tolerance=±5% resistance=100 package="2010 [SMD]"]
  R11 = Resistor [tolerance=±5% resistance=100 package="2010 [SMD]"]
  R12 = Resistor [tolerance=±5% resistance=100 package="2010 [SMD]"]
  Part2 = Arduino Uno (Rev3)
  LCD1 = LCD screen
  KEYPAD1 = Membrane Matrix Keypad
  R13 = Resistor [tolerance=±5% resistance=100 package="2010 [SMD]"]
  R14 = Resistor [tolerance=±5% resistance=330 package=THT]
  LD1 = LD
  LD2 = LD
  LD3 = LD
  KY-1 = Keyes Relay [package=THT]
  KY-6 = Keyes Relay [package=THT]
  KY-7 = Keyes Relay [package=THT]
  KY-8 = Keyes Relay [package=THT]
  KY-9 = Keyes Relay [package=THT]
  LPD8806_RGB_LED_Strip1 = LPD8806 RGB LED Strip
  LPD8806_RGB_LED_Strip2 = LPD8806 RGB LED Strip
  LPD8806_RGB_LED_Strip3 = LPD8806 RGB LED Strip
  LPD8806_RGB_LED_Strip4 = LPD8806 RGB LED Strip
  LPD8806_RGB_LED_Strip5 = LPD8806 RGB LED Strip
  Power_plug1 = Power plug
  Raspberry_Pi1 = Raspberry Pi 2  # not connected
  PIR1 = PIR sensor
  Q3 = PNP-Transistor [part_number=3144 package="SOT-23 [SMD]"]

nets:
  N1: Part1.A0, LCD1.DB6
  N2: Part1.A1, LCD1.DB4
  N3: Part1.A4/SDA, Part2.A4/SDA
  N4: Part1.A5/SCL, Part2.A5/SCL
  N5: Part1.D8, KEYPAD1.6
  N6: Part1.D9_PWM, KEYPAD1.5
  N7: Part1.D10_PWM/SS, KEYPAD1.4
  N8: Part1.D11_PWM/MOSI, KEYPAD1.3
  N9: Part1.D12/MISO, KEYPAD1.2
  N10: Part1.D13/SCK, KEYPAD1.1
  GND: Part1.GND, LCD1.VSS, LCD1.DB5, LCD1.LED-
  N11: Part1.D3_PWM, LCD1.V0
  N12: Part1.D4, LCD1.RS
  N13: Part1.D5_PWM, LCD1.R/W
  N14: Part1.D6_PWM, LCD1.E
  N15: Part1.D7, KEYPAD1.7
  N16: Part1.5V, LCD1.LED+, R13.Pin_0, R14.Pin_1
  5V: R7.P$1, R8.P$1, R9.P$1, Part2.5V, KY-1.power, KY-6.power, KY-7.power, KY-8.power, KY-9.power, PIR1.VDD, Q3.2
  N17: R7.P$2, R12.Pin_1, Part2.A2
  N18: R8.P$2, R11.Pin_1, Part2.A1
  N19: R9.P$2, R10.Pin_1, Part2.A0
  GND_2: R10.Pin_0, R11.Pin_0, R12.Pin_0, Part2.GND, LD1.cathode, LD2.cathode, LD3.cathode, KY-1.ground, KY-6.ground, KY-7.ground, KY-8.ground, KY-9.ground, PIR1.GND, Q3.0
  N20: Part2.D8, KY-7.signal
  N21: Part2.D9_PWM, KY-6.signal
  N22: Part2.D10_PWM/SS, KY-1.signal
  N23: Part2.D11_PWM/MOSI, KY-8.signal
  N24: Part2.D12/MISO, KY-9.signal
  N25: Part2.D2, Q3.1
  N26: Part2.D3_PWM, PIR1.SIG
  N27: Part2.D4, LD1.anode
  N28: Part2.D5_PWM, LD2.anode
  N29: Part2.D6_PWM, LD3.anode
  N30: LCD1.VDD, R14.Pin_0
  N31: LCD1.DB7, R13.Pin_1
  N32: KY-1.NC, LPD8806_RGB_LED_Strip3.+5V
  N33: KY-1.C, KY-6.C, KY-7.C, KY-8.C, KY-9.C, Power_plug1.VCC
  N34: KY-6.NC, LPD8806_RGB_LED_Strip4.+5V
  N35: KY-7.NC, LPD8806_RGB_LED_Strip5.+5V
  N36: KY-8.NC, LPD8806_RGB_LED_Strip2.+5V
  N37: KY-9.NC, LPD8806_RGB_LED_Strip1.+5V
  GND_3: LPD8806_RGB_LED_Strip1.GND, LPD8806_RGB_LED_Strip2.GND, LPD8806_RGB_LED_Strip3.GND, LPD8806_RGB_LED_Strip4.GND, LPD8806_RGB_LED_Strip5.GND, Power_plug1.GND

custom parts:
  Membrane Matrix Keypad: Membrane Matrix 3x4 Keypad
  LD: A Generic Red Dot Laser Diode Module (~5mW)
  Keyes Relay: The Keyes 5V relay module is suitable for SCM development, home appliance control. It uses a 5V~12V TIL control signal which can control DC / AC signal.
  LPD8806 RGB LED Strip: Digitally addressable RGB LED strip
